// Logisim project bunch_of_chips.circ as structural Verilog: 7 circuits, main circuit Game
module Game (
  input  [7:0] Data,
  input  [3:0] Address,
  input  R_W_Selector,
  output [7:0] Dataout
);

  wire _1_out, _2_out, _3_out, _4_out, _5_out, _6_out, C, clock_1_out, H, register_beta_2_clock_2,
       register_beta_2_i_o_mode, register_beta_2_zero, register_beta_3_clock_2, register_beta_3_i_o_mode,
       register_beta_3_zero, register_beta_4_clock_2, register_beta_4_i_o_mode, register_beta_5_clock_2,
       register_beta_5_i_o_mode, register_beta_6_clock_2, register_beta_6_i_o_mode, register_beta_7_clock_2,
       register_beta_7_i_o_mode, register_beta_8_clock_2, register_beta_8_i_o_mode, register_beta_9_clock_2,
       register_beta_9_i_o_mode, register_beta_10_clock_2, register_beta_10_i_o_mode,
       register_beta_11_clock_2, register_beta_11_i_o_mode, register_beta_12_clock_2,
       register_beta_12_i_o_mode, register_beta_13_clock_2, register_beta_13_i_o_mode,
       register_beta_14_clock_2, register_beta_14_i_o_mode;
  wire [3:0] driver_1_out_4, driver_2_out_4, driver_3_out_4, driver_4_out_4, driver_5_out_4, driver_6_out_4,
       increment_1_out_2, register_beta_1_tens, register_beta_1_units, register_beta_2_address_2,
       register_beta_2_position___1, register_beta_2_tens, register_beta_2_units, register_beta_3_address_2,
       register_beta_3_position___1, register_beta_3_tens, register_beta_3_units, register_beta_4_address_2,
       register_beta_4_position___1, register_beta_4_tens, register_beta_4_units, register_beta_5_address_2,
       register_beta_5_position___1, register_beta_5_tens, register_beta_5_units, register_beta_6_address_2,
       register_beta_6_position___1, register_beta_6_tens, register_beta_6_units, register_beta_7_address_2,
       register_beta_7_position___1, register_beta_7_tens, register_beta_7_units, register_beta_8_address_2,
       register_beta_8_position___1, register_beta_8_tens, register_beta_8_units, register_beta_9_address_2,
       register_beta_9_position___1, register_beta_9_tens, register_beta_9_units, register_beta_10_address_2,
       register_beta_10_position___1, register_beta_10_tens, register_beta_10_units,
       register_beta_11_address_2, register_beta_11_position___1, register_beta_11_tens,
       register_beta_11_units, register_beta_12_address_2, register_beta_12_position___1,
       register_beta_12_tens, register_beta_12_units, register_beta_13_address_2,
       register_beta_13_position___1, register_beta_13_tens, register_beta_13_units,
       register_beta_14_address_2, register_beta_14_position___1, register_beta_14_tens,
       register_beta_14_units;
  wire [7:0] register_beta_2_dataout, register_beta_3_dataout, register_beta_4_dataout,
       register_beta_5_dataout, register_beta_6_dataout, register_beta_7_dataout, register_beta_8_dataout,
       register_beta_9_dataout, register_beta_10_dataout, register_beta_11_dataout, register_beta_12_dataout,
       register_beta_13_dataout, register_beta_14_dataout;

  Clock clock_1 (.out(clock_1_out));
  LED led_1 (.in(C));
  LED led_2 (.in(C));
  LED led_3 (.in(C));
  Pull_Resistor pull_resistor_1 (.node(C));
  Hex_Digit_Display hex_digit_display_1 (.value(register_beta_1_tens));  // open: dp
  Register__beta register_beta_1 (
    .Data(register_beta_3_dataout), .Position(register_beta_3_position___1),
    .Address(register_beta_3_address_2), .Clock(register_beta_3_clock_2),
    .O_I_Mode(register_beta_3_i_o_mode), .Dataout(Dataout), .Tens(register_beta_1_tens),
    .Units(register_beta_1_units));  // open: Position___1, Address_2, Clock_2, I_O_Mode, Zero, Driver_Output
  Hex_Digit_Display hex_digit_display_2 (.value(register_beta_1_units));  // open: dp
  Hex_Digit_Display hex_digit_display_3 (.value(register_beta_3_tens));  // open: dp
  Win_Lose_Draw win_lose_draw_1 (
    .Tens(register_beta_1_tens), .Units(register_beta_1_units), .in_3(register_beta_3_zero), .in_4(H),
    .out_5(C));
  Register__beta register_beta_2 (
    .Data(Data), .Position(4'b0000), .Address(Address), .Clock(clock_1_out), .O_I_Mode(R_W_Selector),
    .Position___1(register_beta_2_position___1), .Address_2(register_beta_2_address_2),
    .Clock_2(register_beta_2_clock_2), .I_O_Mode(register_beta_2_i_o_mode),
    .Dataout(register_beta_2_dataout), .Zero(register_beta_2_zero), .Tens(register_beta_2_tens),
    .Units(register_beta_2_units));  // open: Driver_Output
  Hex_Digit_Display hex_digit_display_4 (.value(register_beta_2_tens));  // open: dp
  Hex_Digit_Display hex_digit_display_5 (.value(register_beta_3_units));  // open: dp
  Hex_Digit_Display hex_digit_display_6 (.value(register_beta_2_units));  // open: dp
  Button _1 (.out(_1_out));
  Register__beta register_beta_3 (
    .Data(register_beta_5_dataout), .Position(register_beta_5_position___1),
    .Address(register_beta_5_address_2), .Clock(register_beta_5_clock_2),
    .O_I_Mode(register_beta_5_i_o_mode), .Position___1(register_beta_3_position___1),
    .Address_2(register_beta_3_address_2), .Clock_2(register_beta_3_clock_2),
    .I_O_Mode(register_beta_3_i_o_mode), .Dataout(register_beta_3_dataout), .Zero(register_beta_3_zero),
    .Tens(register_beta_3_tens), .Units(register_beta_3_units));  // open: Driver_Output
  Hex_Digit_Display hex_digit_display_7 (.value(register_beta_5_units));  // open: dp
  Hex_Digit_Display hex_digit_display_8 (.value(register_beta_5_tens));  // open: dp
  Hex_Digit_Display hex_digit_display_9 (.value(register_beta_4_units));  // open: dp
  Register__beta register_beta_4 (
    .Data(register_beta_2_dataout), .Position(register_beta_2_position___1),
    .Address(register_beta_2_address_2), .Clock(register_beta_2_clock_2),
    .O_I_Mode(register_beta_2_i_o_mode), .Position___1(register_beta_4_position___1),
    .Address_2(register_beta_4_address_2), .Clock_2(register_beta_4_clock_2),
    .I_O_Mode(register_beta_4_i_o_mode), .Dataout(register_beta_4_dataout), .Zero(register_beta_2_zero),
    .Tens(register_beta_4_tens), .Units(register_beta_4_units));  // open: Driver_Output
  Hex_Digit_Display hex_digit_display_10 (.value(register_beta_4_tens));  // open: dp
  Driver driver_1 (.out_4(driver_1_out_4), .in_2(driver_2_out_4), .in_3(_1_out));  // open: in_1, out_5
  Button _2 (.out(_2_out));
  Register__beta register_beta_5 (
    .Data(register_beta_7_dataout), .Position(register_beta_7_position___1),
    .Address(register_beta_7_address_2), .Clock(register_beta_7_clock_2),
    .O_I_Mode(register_beta_7_i_o_mode), .Position___1(register_beta_5_position___1),
    .Address_2(register_beta_5_address_2), .Clock_2(register_beta_5_clock_2),
    .I_O_Mode(register_beta_5_i_o_mode), .Dataout(register_beta_5_dataout), .Zero(register_beta_3_zero),
    .Tens(register_beta_5_tens), .Units(register_beta_5_units));  // open: Driver_Output
  Hex_Digit_Display hex_digit_display_11 (.value(register_beta_7_tens));  // open: dp
  Hex_Digit_Display hex_digit_display_12 (.value(register_beta_6_tens));  // open: dp
  Register__beta register_beta_6 (
    .Data(register_beta_4_dataout), .Position(register_beta_4_position___1),
    .Address(register_beta_4_address_2), .Clock(register_beta_4_clock_2),
    .O_I_Mode(register_beta_4_i_o_mode), .Position___1(register_beta_6_position___1),
    .Address_2(register_beta_6_address_2), .Clock_2(register_beta_6_clock_2),
    .I_O_Mode(register_beta_6_i_o_mode), .Dataout(register_beta_6_dataout), .Zero(register_beta_2_zero),
    .Tens(register_beta_6_tens), .Units(register_beta_6_units));  // open: Driver_Output
  Driver driver_2 (.out_4(driver_2_out_4), .in_2(driver_3_out_4), .in_3(_2_out));  // open: in_1, out_5
  Hex_Digit_Display hex_digit_display_13 (.value(register_beta_7_units));  // open: dp
  Hex_Digit_Display hex_digit_display_14 (.value(register_beta_6_units));  // open: dp
  Button _3 (.out(_3_out));
  Register__beta register_beta_7 (
    .Data(register_beta_9_dataout), .Position(register_beta_9_position___1),
    .Address(register_beta_9_address_2), .Clock(register_beta_9_clock_2),
    .O_I_Mode(register_beta_9_i_o_mode), .Position___1(register_beta_7_position___1),
    .Address_2(register_beta_7_address_2), .Clock_2(register_beta_7_clock_2),
    .I_O_Mode(register_beta_7_i_o_mode), .Dataout(register_beta_7_dataout), .Zero(register_beta_3_zero),
    .Tens(register_beta_7_tens), .Units(register_beta_7_units));  // open: Driver_Output
  Hex_Digit_Display hex_digit_display_15 (.value(register_beta_9_tens));  // open: dp
  Hex_Digit_Display hex_digit_display_16 (.value(register_beta_9_units));  // open: dp
  Hex_Digit_Display hex_digit_display_17 (.value(register_beta_8_tens));  // open: dp
  Register__beta register_beta_8 (
    .Data(register_beta_6_dataout), .Position(register_beta_6_position___1),
    .Address(register_beta_6_address_2), .Clock(register_beta_6_clock_2),
    .O_I_Mode(register_beta_6_i_o_mode), .Position___1(register_beta_8_position___1),
    .Address_2(register_beta_8_address_2), .Clock_2(register_beta_8_clock_2),
    .I_O_Mode(register_beta_8_i_o_mode), .Dataout(register_beta_8_dataout), .Zero(register_beta_2_zero),
    .Tens(register_beta_8_tens), .Units(register_beta_8_units));  // open: Driver_Output
  Hex_Digit_Display hex_digit_display_18 (.value(register_beta_8_units));  // open: dp
  Driver driver_3 (.out_4(driver_3_out_4), .in_2(driver_4_out_4), .in_3(_3_out));  // open: in_1, out_5
  Button _4 (.out(_4_out));
  Register__beta register_beta_9 (
    .Data(register_beta_11_dataout), .Position(register_beta_11_position___1),
    .Address(register_beta_11_address_2), .Clock(register_beta_11_clock_2),
    .O_I_Mode(register_beta_11_i_o_mode), .Position___1(register_beta_9_position___1),
    .Address_2(register_beta_9_address_2), .Clock_2(register_beta_9_clock_2),
    .I_O_Mode(register_beta_9_i_o_mode), .Dataout(register_beta_9_dataout), .Zero(register_beta_3_zero),
    .Tens(register_beta_9_tens), .Units(register_beta_9_units));  // open: Driver_Output
  Hex_Digit_Display hex_digit_display_19 (.value(register_beta_11_tens));  // open: dp
  Hex_Digit_Display hex_digit_display_20 (.value(register_beta_10_tens));  // open: dp
  Register__beta register_beta_10 (
    .Data(register_beta_8_dataout), .Position(register_beta_8_position___1),
    .Address(register_beta_8_address_2), .Clock(register_beta_8_clock_2),
    .O_I_Mode(register_beta_8_i_o_mode), .Position___1(register_beta_10_position___1),
    .Address_2(register_beta_10_address_2), .Clock_2(register_beta_10_clock_2),
    .I_O_Mode(register_beta_10_i_o_mode), .Dataout(register_beta_10_dataout), .Zero(register_beta_2_zero),
    .Tens(register_beta_10_tens), .Units(register_beta_10_units));  // open: Driver_Output
  Driver driver_4 (.out_4(driver_4_out_4), .in_2(driver_5_out_4), .in_3(_4_out));  // open: in_1, out_5
  Hex_Digit_Display hex_digit_display_21 (.value(register_beta_11_units));  // open: dp
  Hex_Digit_Display hex_digit_display_22 (.value(register_beta_10_units));  // open: dp
  Button _5 (.out(_5_out));
  Register__beta register_beta_11 (
    .Data(register_beta_13_dataout), .Position(register_beta_13_position___1),
    .Address(register_beta_13_address_2), .Clock(register_beta_13_clock_2),
    .O_I_Mode(register_beta_13_i_o_mode), .Position___1(register_beta_11_position___1),
    .Address_2(register_beta_11_address_2), .Clock_2(register_beta_11_clock_2),
    .I_O_Mode(register_beta_11_i_o_mode), .Dataout(register_beta_11_dataout), .Zero(register_beta_3_zero),
    .Tens(register_beta_11_tens), .Units(register_beta_11_units));  // open: Driver_Output
  Hex_Digit_Display hex_digit_display_23 (.value(register_beta_13_units));  // open: dp
  Hex_Digit_Display hex_digit_display_24 (.value(register_beta_13_tens));  // open: dp
  Hex_Digit_Display hex_digit_display_25 (.value(register_beta_12_units));  // open: dp
  Register__beta register_beta_12 (
    .Data(register_beta_10_dataout), .Position(register_beta_10_position___1),
    .Address(register_beta_10_address_2), .Clock(register_beta_10_clock_2),
    .O_I_Mode(register_beta_10_i_o_mode), .Position___1(register_beta_12_position___1),
    .Address_2(register_beta_12_address_2), .Clock_2(register_beta_12_clock_2),
    .I_O_Mode(register_beta_12_i_o_mode), .Dataout(register_beta_12_dataout), .Zero(register_beta_2_zero),
    .Tens(register_beta_12_tens), .Units(register_beta_12_units));  // open: Driver_Output
  Hex_Digit_Display hex_digit_display_26 (.value(register_beta_12_tens));  // open: dp
  Driver driver_5 (.out_4(driver_5_out_4), .in_2(driver_6_out_4), .in_3(_5_out));  // open: in_1, out_5
  Button _6 (.out(_6_out));
  Register__beta register_beta_13 (
    .Data(register_beta_14_dataout), .Position(increment_1_out_2), .Address(register_beta_14_address_2),
    .Clock(register_beta_14_clock_2), .O_I_Mode(register_beta_14_i_o_mode),
    .Position___1(register_beta_13_position___1), .Address_2(register_beta_13_address_2),
    .Clock_2(register_beta_13_clock_2), .I_O_Mode(register_beta_13_i_o_mode),
    .Dataout(register_beta_13_dataout), .Zero(register_beta_3_zero), .Tens(register_beta_13_tens),
    .Units(register_beta_13_units));  // open: Driver_Output
  Pull_Resistor #(.pull(1)) pull_resistor_2 (.node(register_beta_3_zero));
  Win_Lose_Draw win_lose_draw_2 (
    .Tens(register_beta_14_tens), .Units(register_beta_14_units), .in_3(register_beta_2_zero), .in_4(C),
    .out_5(H));
  Pull_Resistor #(.pull(1)) pull_resistor_3 (.node(register_beta_2_zero));
  Driver driver_6 (.out_4(driver_6_out_4), .in_3(_6_out));  // open: in_2, in_1, out_5
  Hex_Digit_Display hex_digit_display_27 (.value(register_beta_14_tens));  // open: dp
  Register__beta register_beta_14 (
    .Data(register_beta_12_dataout), .Position(register_beta_12_position___1),
    .Address(register_beta_12_address_2), .Clock(register_beta_12_clock_2),
    .O_I_Mode(register_beta_12_i_o_mode), .Position___1(register_beta_14_position___1),
    .Address_2(register_beta_14_address_2), .Clock_2(register_beta_14_clock_2),
    .I_O_Mode(register_beta_14_i_o_mode), .Dataout(register_beta_14_dataout), .Tens(register_beta_14_tens),
    .Units(register_beta_14_units));  // open: Zero, Driver_Output
  Increment increment_1 (.in_1(register_beta_14_position___1), .out_2(increment_1_out_2));
  LED led_4 (.in(H));
  LED led_5 (.in(H));
  LED led_6 (.in(H));
  Hex_Digit_Display hex_digit_display_28 (.value(register_beta_14_units));  // open: dp
  Pull_Resistor pull_resistor_4 (.node(H));
endmodule

module Register__alpha (
  input  [7:0] mypos,
  input  [3:0] in_2,
  input  [3:0] in_3,
  input  in_4,
  input  in_5,
  output [7:0] out_6,
  output [3:0] out_7,
  output [3:0] out_8,
  output [3:0] out_9,
  output out_10,
  output out_11,
  output Zero,
  output [3:0] Tens,
  output [3:0] Units
);

  wire and_1_out, and_2_out, comparator_1_eq;
  wire [4:0] bitselector_1_out, divider_1_out, divider_1_rem;
  wire [5:0] register_1_q;
  wire [7:0] bit_extender_1_out, controlled_buffer_1_out, transistor_1_out;

  Adder #(.width(4)) adder_1 (.a(in_2), .b(4'b0001), .out(out_7));  // open: cin, cout
  and and_1 (and_1_out, comparator_1_eq, in_5);
  Comparator #(.width(4)) comparator_1 (.a(out_7), .b(in_3), .eq(comparator_1_eq));  // open: gt, lt
  assign controlled_buffer_1_out = and_1_out ? mypos : 8'bz;  // Controlled_Buffer controlled_buffer_1
  BitSelector #(.group(5)) bitselector_1 (.in(controlled_buffer_1_out), .out(bitselector_1_out), .sel(1'b0));
  Register #(.width(5), .trigger("falling")) register_1 (
    .D(bitselector_1_out), .Q(register_1_q[4:0]), .clk(in_4));  // open: en, clr
  and and_2 (and_2_out, comparator_1_eq, in_4, in_5);
  Multiplexer #(.width(8)) multiplexer_1 (
    .in0(mypos), .in1(transistor_1_out), .out(out_6), .sel(and_2_out));  // open: en
  Transistor #(.\type ("n"), .width(8)) transistor_1 (
    .in(bit_extender_1_out), .out(transistor_1_out), .gate(and_2_out));
  assign bit_extender_1_out = {{3{1'b0}}, register_1_q[4:0]};  // Bit_Extender bit_extender_1
  Not_Null not_null_1 (.in_1(register_1_q), .out_2(Zero));
  Divider #(.width(5)) divider_1 (
    .a(register_1_q[4:0]), .b(5'b01010), .out(divider_1_out), .rem(divider_1_rem));  // open: upper
  Bit_Extender #(.in_width(5), .out_width(4)) bit_extender_2 (.in(divider_1_out), .out(Tens));
  Bit_Extender #(.in_width(5), .out_width(4)) bit_extender_3 (.in(divider_1_rem), .out(Units));
  // Pins of 5 and 6 bits meet at register_1_q

  assign out_8 = in_3;
  assign out_9 = out_7;
  assign out_10 = in_4;
  assign out_11 = in_5;

  // Notes on the sheet:
  //   data
  //   pos
  //   addr
  //   clock
  //   dir
  //   WEST
  //   register content
  //   out_condition
  //   EAST
  //   SOUTH
  //   NORTH
  //   position for btn driver
endmodule

module Register__beta (
  input  [7:0] Data,
  input  [3:0] Position,
  input  [3:0] Address,
  input  Clock,
  input  O_I_Mode,
  output [7:0] Dataout,
  output [3:0] Position___1,
  output [3:0] Driver_Output,
  output [3:0] Address_2,
  output Clock_2,
  output I_O_Mode,
  output Zero,
  output [3:0] Tens,
  output [3:0] Units
);

  wire and_1_out, Data_selector, not_1_out, Target;
  wire [5:0] bit_extender_1_out, divider_1_out, divider_1_rem, register_1_q;
  wire [7:0] Register_value;

  Increment increment_1 (.in_1(Position), .out_2(Driver_Output));
  Bit_Extender #(.out_width(6)) bit_extender_1 (.in(Data), .out(bit_extender_1_out));
  and and_1 (and_1_out, Clock, O_I_Mode, Target);
  Divider #(.width(6)) divider_1 (
    .a(register_1_q), .b(6'b001010), .out(divider_1_out), .rem(divider_1_rem));  // open: upper
  Register #(.width(6)) register_1 (.D(bit_extender_1_out), .Q(register_1_q), .clk(and_1_out));  // open: en, clr
  Not_Null not_null_1 (.in_1(register_1_q), .out_2(Zero));
  Multiplexer #(.width(8), .enable("false")) multiplexer_1 (
    .in0(Data), .in1(Register_value), .out(Dataout), .sel(Data_selector));
  Comparator #(.width(4)) comparator_1 (.a(Driver_Output), .b(Address), .eq(Target));  // open: gt, lt
  assign Register_value = {{2{1'b0}}, register_1_q};  // Bit_Extender bit_extender_2
  not not_1 (not_1_out, O_I_Mode);
  Bit_Extender #(.in_width(6), .out_width(4)) bit_extender_3 (.in(divider_1_out), .out(Tens));
  Bit_Extender #(.in_width(6), .out_width(4)) bit_extender_4 (.in(divider_1_rem), .out(Units));
  and and_2 (Data_selector, not_1_out, Target);

  assign Address_2 = Address;
  assign Clock_2 = Clock;
  assign I_O_Mode = O_I_Mode;
  assign Position___1 = Driver_Output;
endmodule

module Driver (
  input  [3:0] in_1,
  input  [3:0] in_2,
  input  in_3,
  output [3:0] out_4,
  output out_5
);

  assign in_2 = in_3 ? in_1 : 4'bz;  // Controlled_Buffer controlled_buffer_1
  Transistor #(.\type ("n")) transistor_1 (.in(1'b0), .out(out_5), .gate(in_3));

  assign out_4 = in_2;
endmodule

module Win_Lose_Draw (
  input  [3:0] Tens,
  input  [3:0] Units,
  input  in_3,
  input  in_4,
  output out_5
);

  wire comparator_1_eq, comparator_1_gt, or_1_out, or_2_out, or_3_out;
  wire [7:0] adder_1_out, bit_extender_1_out, bit_extender_2_out, multiplier_1_out, register_1_q;

  assign bit_extender_1_out = {{4{1'b0}}, Tens};  // Bit_Extender bit_extender_1
  assign bit_extender_2_out = {{4{1'b0}}, Units};  // Bit_Extender bit_extender_2
  Multiplier multiplier_1 (.a(8'ha), .b(bit_extender_1_out), .out(multiplier_1_out));  // open: cin, cout
  Register #(.trigger("falling")) register_1 (.D(adder_1_out), .Q(register_1_q), .clk(in_3));  // open: en, clr
  Adder adder_1 (.a(multiplier_1_out), .b(bit_extender_2_out), .out(adder_1_out));  // open: cin, cout
  Comparator comparator_1 (.a(register_1_q), .b(8'h18), .gt(comparator_1_gt), .eq(comparator_1_eq));  // open: lt
  or or_1 (or_1_out, register_1_q[0], register_1_q[1], register_1_q[2], register_1_q[3], register_1_q[4], register_1_q[5], register_1_q[6], register_1_q[7]);
  or or_2 (or_2_out, comparator_1_gt, comparator_1_eq);
  or or_3 (or_3_out, in_4, or_1_out);
  and and_1 (out_5, or_2_out, or_3_out);
endmodule

module Increment (
  input  [3:0] in_1,
  output [3:0] out_2
);

  Adder #(.width(4)) adder_1 (.a(in_1), .b(4'b0001), .out(out_2));  // open: cin, cout
endmodule

module Not_Null (
  input  [5:0] in_1,
  output out_2
);

  wire or_1_out;

  or or_1 (or_1_out, in_1[0], in_1[1], in_1[2], in_1[3], in_1[4], in_1[5]);
  Transistor #(.\type ("n")) transistor_1 (.in(1'b0), .out(out_2), .gate(or_1_out));
endmodule
