// Logisim project display.circ as structural Verilog: 2 circuits, main circuit Button Driver
module Button_Driver (
  input  [3:0] Position,
  input  [3:0] Address,
  input  Is_Zero,
  input  Button,
  output [3:0] Address_2,
  output Trigger
);

  wire not_1_out, pull_resistor_1_node;

  assign Address_2 = pull_resistor_1_node ? Position : 4'bz;  // Controlled_Buffer controlled_buffer_1
  assign Address_2 = not_1_out ? Address : 4'bz;  // Controlled_Buffer controlled_buffer_2
  Pull_Resistor pull_resistor_1 (.node(pull_resistor_1_node));
  Transistor transistor_1 (.in(Button), .out(pull_resistor_1_node), .gate(Is_Zero));
  Pull_Resistor #(.pull(1)) pull_resistor_2 (.node(Is_Zero));
  not not_1 (not_1_out, pull_resistor_1_node);
  Transistor #(.\type ("n")) transistor_2 (.in(1'b0), .out(Trigger), .gate(pull_resistor_1_node));
endmodule

module Button_Register (
  input  [7:0] Data,
  input  [3:0] Position,
  input  [3:0] Address,
  input  Clock,
  input  R___W_Selector,
  output [7:0] Dataout,
  output [3:0] Position___1,
  output [3:0] Address_2,
  output [3:0] Driver,
  output Clock_2,
  output R___W_Selector_2,
  output Zero,
  output [3:0] Tens,
  output [3:0] Units,
  output Zero_2
);

  wire Dataout_Selector, Target, W_out;
  wire [5:0] bit_extender_1_out, divider_1_out, divider_1_rem, register_1_q;
  wire [7:0] bit_extender_2_out;

  Bit_Extender #(.out_width(6)) bit_extender_1 (.in(Data), .out(bit_extender_1_out));
  and W (W_out, ~R___W_Selector, Target);  // AND_Gate
  Increment__4_bits increment_4_bits_1 (.in_1(Position), .out_2(Driver));
  Register #(.width(6)) register_1 (.D(bit_extender_1_out), .en(W_out), .Q(register_1_q), .clk(Clock));  // open: clr
  assign bit_extender_2_out = {{2{1'b0}}, register_1_q};  // Bit_Extender bit_extender_2
  Not_Zero__6_bits not_zero_6_bits_1 (.in_1(register_1_q), .out_2(Zero));
  Divider #(.width(6)) divider_1 (
    .a(register_1_q), .b(6'b001010), .out(divider_1_out), .rem(divider_1_rem));  // open: upper
  Multiplexer #(.width(8), .enable("false")) multiplexer_1 (
    .in0(Data), .in1(bit_extender_2_out), .out(Dataout), .sel(Dataout_Selector));
  Is_Equal__4_bits is_equal_4_bits_1 (.A(Driver), .B(Address), .R(Target));
  and and_1 (Dataout_Selector, R___W_Selector, Target);
  Bit_Extender #(.in_width(6), .out_width(4)) bit_extender_3 (.in(divider_1_out), .out(Tens));
  Bit_Extender #(.in_width(6), .out_width(4)) bit_extender_4 (.in(divider_1_rem), .out(Units));

  assign Address_2 = Address;
  assign Clock_2 = Clock;
  assign Position___1 = Driver;
  assign R___W_Selector_2 = R___W_Selector;
  assign Zero_2 = Zero;
endmodule
