// Logisim project judge.circ as structural Verilog: 2 circuits, main circuit Win-Lose-Draw, beta
module Win_Lose_Draw__beta (
  input  [3:0] Tens,
  input  [3:0] Units,
  input  Is_Zero,
  input  Another,
  output out_5,
  output out_6
);

  wire comparator_1_gt, xor_1_out;
  wire [7:0] adder_1_out, bit_extender_1_out, bit_extender_2_out, multiplier_1_out, register_1_q;

  assign bit_extender_1_out = {{4{1'b0}}, Tens};  // Bit_Extender bit_extender_1
  assign bit_extender_2_out = {{4{1'b0}}, Units};  // Bit_Extender bit_extender_2
  xor xor_1 (xor_1_out, Is_Zero, Another);
  Multiplier multiplier_1 (.a(8'ha), .b(bit_extender_1_out), .out(multiplier_1_out));  // open: cin, cout
  Adder adder_1 (.a(multiplier_1_out), .b(bit_extender_2_out), .out(adder_1_out));  // open: cin, cout
  Register register_1 (.D(adder_1_out), .Q(register_1_q), .clk(xor_1_out));  // open: en, clr
  Comparator comparator_1 (.a(register_1_q), .b(8'h18), .gt(comparator_1_gt), .eq(out_6));  // open: lt
  or or_1 (out_5, comparator_1_gt, out_6);

  // Notes on the sheet:
  //   Another: pull=down
endmodule

module Win_Lose_Draw__omega (
  input  [3:0] Units,
  input  [3:0] Tens,
  input  [7:0] Helper,
  output Draw,
  output Win,
  output [7:0] Helper_2
);

  wire pull_resistor_2_node;
  wire [7:0] adder_2_out, bit_extender_1_out, bit_extender_2_out, multiplier_1_out, pull_resistor_1_node;

  assign bit_extender_1_out = {{4{1'b0}}, Units};  // Bit_Extender bit_extender_1
  assign bit_extender_2_out = {{4{1'b0}}, Tens};  // Bit_Extender bit_extender_2
  Multiplier multiplier_1 (.a(bit_extender_2_out), .b(8'ha), .out(multiplier_1_out));  // open: cin, cout
  Pull_Resistor pull_resistor_1 (.node(pull_resistor_1_node));
  assign pull_resistor_1_node = pull_resistor_2_node ? Helper_2 : 8'bz;  // Controlled_Buffer controlled_buffer_1
  Adder adder_1 (.a(bit_extender_1_out), .b(multiplier_1_out), .out(Helper_2));  // open: cin, cout
  Comparator comparator_1 (.a(8'h18), .b(pull_resistor_1_node), .eq(Draw), .lt(Win));  // open: gt
  Adder adder_2 (.a(Helper_2), .b(Helper), .out(adder_2_out));  // open: cin, cout
  Pull_Resistor pull_resistor_2 (.node(pull_resistor_2_node));
  Comparator #(.mode("unsigned")) comparator_2 (.a(8'h30), .b(adder_2_out), .eq(pull_resistor_2_node));  // open: gt, lt
endmodule
