// Logisim project utility.circ as structural Verilog: 10 circuits, main circuit Increment (4 bits)
module Gamepad_Address_Manager (
  input  [7:0] Input_Address,
  input  Data,
  output [3:0] Gamepad_Address,
  output Is_Selected
);

  wire comparator_1_lt;
  wire [3:0] bit_extender_1_out;

  Comparator #(.mode("unsigned")) comparator_1 (.a(8'hf0), .b(Input_Address), .lt(comparator_1_lt));  // open: gt, eq
  Bit_Extender #(.out_width(4)) bit_extender_1 (.in(Input_Address), .out(bit_extender_1_out));
  and and_1 (Is_Selected, comparator_1_lt, Data);
  assign Gamepad_Address = Is_Selected ? bit_extender_1_out : 4'bz;  // Controlled_Buffer controlled_buffer_1
  Pull_Resistor pull_resistor_1 (.node(Gamepad_Address));
endmodule

module RAM_Address_Manager (
  input  [7:0] Input_Address,
  input  Data,
  output [3:0] RAM_Address,
  output Is_Selected
);

  wire and_1_out, comparator_1_lt, comparator_2_gt;
  wire [3:0] bit_extender_1_out;

  Comparator #(.mode("unsigned")) comparator_1 (.a(Input_Address), .b(8'hf0), .lt(comparator_1_lt));  // open: gt, eq
  Comparator #(.mode("unsigned")) comparator_2 (.a(Input_Address), .b(8'hdf), .gt(comparator_2_gt));  // open: eq, lt
  Bit_Extender #(.out_width(4)) bit_extender_1 (.in(Input_Address), .out(bit_extender_1_out));
  and and_1 (and_1_out, comparator_1_lt, comparator_2_gt);
  assign RAM_Address = Is_Selected ? bit_extender_1_out : 4'bz;  // Controlled_Buffer controlled_buffer_1
  and and_2 (Is_Selected, and_1_out, Data);
endmodule

module Memory_Manager (
  input  [7:0] Data,
  input  Data_2,
  input  Clock,
  input  [7:0] Address,
  input  [7:0] Control_Byte,
  output A,
  output B,
  output C,
  output D
);

  wire and_1_out, is_equal_8_bits_1_r;
  wire [1:0] bit_extender_1_out, register_1_q;

  Is_Equal__8_bits is_equal_8_bits_1 (.A(Address), .B(Control_Byte), .R(is_equal_8_bits_1_r));
  Bit_Extender #(.out_width(2)) bit_extender_1 (.in(Data), .out(bit_extender_1_out));
  and and_1 (and_1_out, Data_2, is_equal_8_bits_1_r);
  Register #(.width(2)) register_1 (
    .D(bit_extender_1_out), .en(and_1_out), .Q(register_1_q), .clk(Clock));  // open: clr
  Decoder #(.select(2), .disabled(0), .enable("false")) decoder_1 (
    .out0(A), .out1(B), .out2(C), .out3(D), .sel(register_1_q));
endmodule

module User_Input_Register (
  input  [3:0] User_Input,
  input  [7:0] Program_Input,
  input  R___W,
  input  [7:0] Address,
  input  Data,
  output [7:0] Output,
  output Is_Active
);

  wire and_1_out, and_2_out, and_3_out, is_equal_8_bits_1_r, is_equal_8_bits_2_r;
  wire [7:0] bit_extender_1_out, register_1_q;

  assign bit_extender_1_out = {{4{1'b1}}, User_Input};  // Bit_Extender bit_extender_1
  assign bit_extender_1_out = and_1_out ? Program_Input : 8'bz;  // Controlled_Buffer controlled_buffer_1
  Is_Equal__8_bits is_equal_8_bits_1 (.A({8{1'b1}}), .B(register_1_q), .R(is_equal_8_bits_1_r));
  Is_Equal__8_bits is_equal_8_bits_2 (.A(Address), .B(8'hf8), .R(is_equal_8_bits_2_r));
  Register #(.trigger("low")) register_1 (
    .D(bit_extender_1_out), .en(Is_Active), .Q(register_1_q), .clk(1'b0));  // open: clr
  or or_1 (Is_Active, is_equal_8_bits_1_r, and_1_out);
  and and_1 (and_1_out, ~R___W, and_2_out);  // AND_Gate
  and and_2 (and_2_out, is_equal_8_bits_2_r, Data);
  assign Output = and_3_out ? register_1_q : 8'bz;  // Controlled_Buffer controlled_buffer_2
  and and_3 (and_3_out, R___W, and_2_out);
endmodule

module Big_Controlled_Buffer (
  input  A,
  input  B,
  input  C,
  input  D,
  input  Control,
  output A_2,
  output B_2,
  output \С ,
  output D_2
);

  Transistor #(.\type ("n"), .gate("br")) transistor_1 (.in(A), .out(A_2), .gate(Control));
  Transistor #(.\type ("n"), .gate("br")) transistor_2 (.in(B), .out(B_2), .gate(Control));
  Transistor #(.\type ("n"), .gate("br")) transistor_3 (.in(C), .out(\С ), .gate(Control));
  Pull_Resistor pull_resistor_1 (.node(A_2));
  Pull_Resistor pull_resistor_2 (.node(B_2));
  Pull_Resistor pull_resistor_3 (.node(\С ));
  Pull_Resistor pull_resistor_4 (.node(D_2));
  Transistor #(.\type ("n"), .gate("br")) transistor_4 (.in(D), .out(D_2), .gate(Control));
endmodule

module Increment__4_bits (
  input  [3:0] in_1,
  output [3:0] out_2
);

  Adder #(.width(4)) adder_1 (.a(in_1), .b(4'b0001), .out(out_2));  // open: cin, cout
endmodule

module Swapper__4_btis (
  input  [3:0] A,
  input  [3:0] B,
  output [3:0] B_2,
  output [3:0] A_2
);


  assign A_2 = B;
  assign B_2 = A;
endmodule

module Is_Equal__4_bits (
  input  [3:0] A,
  input  [3:0] B,
  output R
);

  Comparator #(.width(4)) comparator_1 (.a(A), .b(B), .eq(R));  // open: gt, lt
endmodule

module Is_Equal__8_bits (
  input  [7:0] A,
  input  [7:0] B,
  output R
);

  Comparator comparator_1 (.a(A), .b(B), .eq(R));  // open: gt, lt
endmodule

module Not_Zero__6_bits (
  input  [5:0] in_1,
  output out_2
);

  wire or_1_out;

  or or_1 (or_1_out, in_1[0], in_1[1], in_1[2], in_1[3], in_1[4], in_1[5]);
  Transistor #(.\type ("n")) transistor_1 (.in(1'b0), .out(out_2), .gate(or_1_out));
endmodule
